# Fritzing sketch Untitled Sketch (saved by Fritzing 0.9.3b)
circuit board: 8.46667cm x 5.64444cm
breadboards: 1

parts:
  U1 = Arduino Due (Rev2b)
  DRV_1 = DRV 8825 Stepper Motor Carrier, High Current [part_number="DRV 8825"]
  DRV_2 = DRV 8825 Stepper Motor Carrier, High Current [part_number="DRV 8825"]
  DRV_3 = DRV 8825 Stepper Motor Carrier, High Current [part_number="DRV 8825"]
  DRV_4 = DRV 8825 Stepper Motor Carrier, High Current [part_number="DRV 8825"]
  Part1 = Bluetooth HC-05 Macho
  M2 = Stepper Motor - Bipolar
  C1 = Ceramic Capacitor [capacitance=1µF package="100 mil [THT, multilayer]"]
  C2 = Ceramic Capacitor [capacitance=1µF package="100 mil [THT, multilayer]"]
  C3 = Ceramic Capacitor [capacitance=1µF package="100 mil [THT, multilayer]"]
  C4 = Ceramic Capacitor [capacitance=1µF package="100 mil [THT, multilayer]"]
  M3 = Stepper Motor - Bipolar
  M4 = Stepper Motor - Bipolar
  M5 = Stepper Motor - Bipolar
  JP2 = Header 2 [package=screwterminal-3.5mm-2_lock]
  Part2 = Digital Temperature Sensor Breakout - TMP102
  C5 = Ceramic Capacitor [capacitance=3.3µF package="100 mil [THT, multilayer]"]
  C6 = Ceramic Capacitor [capacitance=3.3µF package="100 mil [THT, multilayer]"]
  Q1 = NPN-Transistor [package="TO92 [THT]"]

nets:
  N1: U1.D20/SDA3, Part2.SDA
  N2: U1.D21/SCL3, Part2.SCL
  N3: U1.IOREF, Part1.VCC, Part2.V+, Part2.ADD0
  N4: U1.5V, DRV_2.MS1, DRV_2.MS2, DRV_2.MS3, DRV_2.RESET, DRV_3.MS1, DRV_4.MS1, DRV_4.MS2, DRV_4.MS3, DRV_4.RESET, C6.1, Q1.C
  GND: U1.GND, DRV_1.ENABLE, DRV_1.GROUND_LOG, DRV_2.ENABLE, DRV_2.GROUND_ST/_MT, DRV_2.GROUND_LOG, DRV_3.ENABLE, DRV_3.GROUND_ST/_MT, DRV_3.GROUND_LOG, DRV_4.ENABLE, DRV_4.GROUND_ST/_MT, DRV_4.GROUND_LOG, Part1.GND, C1.0, C3.0, C4.0, JP2.1, Part2.GND, C5.0, C6.0
  N5: U1.VIN, DRV_1.VOLTAGE_ST/_MT, DRV_2.VOLTAGE_ST/_MT, DRV_3.VOLTAGE_ST/_MT, DRV_4.VOLTAGE_ST/_MT, C1.1, C2.1, C3.1, C4.1, JP2.2, C5.1
  N6: U1.D8_PWM, DRV_4.DIRECTION
  N7: U1.D9_PWM, DRV_4.STEP
  N8: U1.D10_PWM/SS0, DRV_3.DIRECTION
  N9: U1.D11_PWM, DRV_3.STEP
  N10: U1.D13_PWM, Q1.B
  N11: U1.D0/RX, Part1.RXD
  N12: U1.D1/TX, Part1.TXD
  N13: U1.D4_PWM/SS1, DRV_1.DIRECTION
  N14: U1.D5_PWM, DRV_1.STEP
  N15: U1.D6_PWM, DRV_2.DIRECTION
  N16: U1.D7_PWM, DRV_2.STEP
  N17: DRV_1.MS1, DRV_1.MS2, DRV_1.MS3, DRV_1.RESET, DRV_3.MS2, DRV_3.MS3, DRV_3.RESET
  N18: DRV_1.SLEEP, DRV_2.SLEEP, DRV_3.SLEEP, DRV_4.SLEEP, Q1.E
  N19: DRV_1.GROUND_ST/_MT, C2.0
  N20: DRV_1.OUT_2B, M4.A
  N21: DRV_1.OUT_2A, M4.B
  N22: DRV_1.OUT_1A, M4.D
  N23: DRV_1.OUT_1B, M4.C
  N24: DRV_2.OUT_2B, M5.A
  N25: DRV_2.OUT_2A, M5.B
  N26: DRV_2.OUT_1A, M5.D
  N27: DRV_2.OUT_1B, M5.C
  N28: DRV_3.OUT_2B, M2.A
  N29: DRV_3.OUT_2A, M2.B
  N30: DRV_3.OUT_1A, M2.D
  N31: DRV_3.OUT_1B, M2.C
  N32: DRV_4.OUT_2B, M3.A
  N33: DRV_4.OUT_2A, M3.B
  N34: DRV_4.OUT_1A, M3.D
  N35: DRV_4.OUT_1B, M3.C
